# Fritzing sketch tricolorLEDProtoBoardLayout (saved by Fritzing 0.9.3b)
breadboards: 1

parts:
  Teensy_3_1 = Teensy 3.1  # not connected
  LED1 = RGB LED (com. cathode, rgb) [package="5 mm [THT]"]
  R1 = Resistor [tolerance=±5% resistance=220 package="2512 [SMD]"]
  R2 = Resistor [tolerance=±5% resistance=220 package="2512 [SMD]"]
  R3 = Resistor [tolerance=±5% resistance=220 package="2512 [SMD]"]

nets:
  N1: LED1.red_anode, R1.Pin_1
  N2: LED1.green_anode, R2.Pin_1
  N3: LED1.blue_anode, R3.Pin_1

notes:
  CST8227 - Interfacing
  Lab 03 - PWM
  Tricolour LED: Red, Green, Blue
  Notes:
  * use PWM pins on the Teensy
  * this circuit is for demo 1 and 2; you'll need to add a pushbutton for demos 3 and 4
  Gerald.Hurdle@AlgonquinCollege.com
