# Fritzing sketch lab6_demo1 (saved by Fritzing 0.9.4)
breadboards: 1

parts:
  Teensy1 = Teensy 3.0  # not connected
  R1 = Trimmer Potentiometer [maximum_resistance=10kΩ package=THT]
  R2 = Resistor [tolerance=±5% resistance=220 package=THT]
  R3 = Resistor [tolerance=±5% resistance=220 package=THT]
  R4 = Resistor [tolerance=±5% resistance=220 package=THT]
  LED1 = RGB LED (com. cathode, rgb) [package="5 mm [THT]"]

nets:
  N1: R1.leg1, LED1.common_cathode
  N2: R2.Pin_0, LED1.red_anode
  N3: R3.Pin_0, LED1.green_anode
  N4: R4.Pin_0, LED1.blue_anode

notes:
  @author Patrick Bobyn (boby0003)
