# Fritzing sketch IoT-led (saved by Fritzing 0.9.3b)
breadboards: 1

parts:
  Teensy_3_1 = Teensy 3.1  # not connected
  R1 = Resistor [tolerance=±5% resistance=220 package="2512 [SMD]"]
  R4 = Resistor [tolerance=±5% resistance=220 package="2512 [SMD]"]
  S1 = Pushbutton [package="[THT]"]
  LED1 = LED - 5mm [color="Red (633nm)" package="5 mm [THT]"]

nets:
  N1: R1.Pin_0, LED1.anode
  N2: R4.Pin_0, S1.Pin_1, S1.Pin_2
  N3: R4.Pin_1, LED1.cathode
  N4: S1.Pin_3, S1.Pin_4

notes:
  CST8227 - Interfacing
  Internet of Things (IoT)
  Discrete LED with push button switch (PBS) in pull-down configuration.
  Instructions:
  1) Build this circuit.
  2) Upload 'Standard Firmata Plus' to your Teensy; quit Arduino IDE and Teensy Loader.
  3) Run node-red
  Gerald.Hurdle@AlgonquinCollege.com
