# Fritzing sketch IoT-tricolor-led (saved by Fritzing 0.9.3b)
breadboards: 1

parts:
  Teensy_3_1 = Teensy 3.1  # not connected
  R1 = Resistor [tolerance=±5% resistance=220 package="2512 [SMD]"]
  R2 = Resistor [tolerance=±5% resistance=220 package="2512 [SMD]"]
  R3 = Resistor [tolerance=±5% resistance=220 package="2512 [SMD]"]
  R4 = Resistor [tolerance=±5% resistance=220 package="2512 [SMD]"]
  S1 = Pushbutton [package="[THT]"]
  LED1 = RGB LED (com. cathode, rbg) [package="5 mm [THT]"]

nets:
  N1: R1.Pin_1, LED1.green_anode
  N2: R2.Pin_1, LED1.blue_anode
  N3: R3.Pin_1, LED1.red_anode
  N4: R4.Pin_0, S1.Pin_1, S1.Pin_2
  N5: R4.Pin_1, LED1.common_cathode
  N6: S1.Pin_3, S1.Pin_4

notes:
  CST8227 - Interfacing
  Internet of Things (IoT)
  Tri-Color LED with push button switch (PBS) in pull-down configuration.
  Instructions:
  1) Build this circuit.
  2) Upload 'Standard Firmata Plus' to your Teensy; quit Arduino IDE and Teensy Loader.
  3) Run node-red
  Gerald.Hurdle@AlgonquinCollege.com
